# Fritzing sketch Freemometer (saved by Fritzing 0.7.5b)
breadboards: 1

parts:
  Nano1 = Arduino Nano v2.3
  Ringer_Motor = DC Motor
  Q1 = NPN-Transistor [package="TO92 [THT]"]
  Ringer_Cap = Electrolytic Capacitor [capacitance=1µF package="100 mil [THT, electrolytic]"]
  D1 = Rectifier Diode [part_number=1N4001 package="300 mil [THT]"]
  LED3 = LED - 5mm [color="Green (565nm)" package="5 mm [THT]"]
  LED4 = LED - 5mm [color="Red (633nm)" package="5 mm [THT]"]
  J1 = Basic Servo

nets (from the schematic view):
  GND: Nano1.GND, Q1.E, J1.gnd
  N1: Nano1.D7, Q1.B
  N2: Nano1.D10, J1.pulse
  N3: Nano1.D12, LED3.anode, LED4.cathode
  N4: Nano1.D13, LED3.cathode, LED4.anode
  +5V: Nano1.+5V, Ringer_Motor.pin_1, Ringer_Cap.+, D1.cathode, J1.vcc
  N5: Ringer_Motor.pin_2, Q1.C, Ringer_Cap.-, D1.anode

notes:
  Ringer and Cap
  Come with Dekad
  Servo Controls Dial
  Single Red/Green LED
