# Fritzing sketch ti launchpad (saved by Fritzing 0.7.5b)
breadboards: 1

parts:
  Common_Anode_RGB_LED = RGB LED (com. anode, rbg) [package="5 mm [THT]"]
  R1 = Resistor [tolerance=±5% resistance=100 package=THT]
  R2 = Resistor [tolerance=±5% resistance=100 package=THT]
  R3 = Resistor [tolerance=±5% resistance=100 package=THT]

nets:
  N1: Common_Anode_RGB_LED.red_cathode, R1.Pin_0
  3.3V: Common_Anode_RGB_LED.common_anode
  N2: Common_Anode_RGB_LED.blue_cathode, R3.Pin_0
  N3: Common_Anode_RGB_LED.green_cathode, R2.Pin_0

notes:
  P1.6
  P2_2
  P2_5
